// Logisim project 11920232202561+芦思瑶+第一次实验设计文件.circ as structural Verilog: 1 circuit, main circuit main
module main (
  input  A,
  input  B,
  input  C,
  input  D,
  input  A_2,
  input  B_2,
  input  C_2,
  input  D_2,
  input  X,
  input  Y,
  input  Z,
  output out_12,
  output out_13,
  output out_14,
  output out_15,
  output out_16,
  output out_17,
  output out_18,
  output out_19,
  output out_20,
  output out_21,
  output out_22,
  output out_23,
  output out_24,
  output out_25,
  output out_26,
  output out_27,
  output out_28,
  output out_29,
  output out_30,
  output out_31,
  output out_32
);

  wire A_t, and_1_out, and_2_out, and_3_out, and_4_out, and_5_out, and_6_out, and_7_out, and_8_out,
       and_9_out, and_10_out, and_11_out, and_12_out, and_13_out, and_14_out, and_15_out, and_16_out,
       and_17_out, and_18_out, and_19_out, and_20_out, and_21_out, and_22_out, and_23_out, and_24_out,
       and_25_out, and_26_out, and_27_out, and_28_out, and_29_out, and_32_out, and_33_out, and_34_out,
       and_35_out, and_36_out, and_37_out, and_38_out, and_39_out, and_40_out, and_41_out, and_42_out,
       and_43_out, and_44_out, and_45_out, and_46_out, and_47_out, and_48_out, and_50_out, and_51_out,
       and_52_out, and_53_out, and_54_out, and_55_out, and_56_out, and_57_out, and_58_out, button_1_out,
       button_2_out, button_3_out, button_4_out, button_5_out, button_6_out, button_7_out, button_8_out,
       button_9_out, buzzer_1_p1, buzzer_5_p1, buzzer_7_p1, buzzer_9_p1, buzzer_10_p1, buzzer_11_p1,
       buzzer_13_p1, buzzer_15_p1, clock_1_out, clock_2_out, clock_3_out, clock_4_out, clock_5_out,
       clock_6_out, clock_7_out, clock_8_out, clock_9_out, comparator_1_eq, comparator_4_eq, comparator_5_eq,
       comparator_6_eq, comparator_7_eq, comparator_8_eq, comparator_9_eq, comparator_10_eq,
       comparator_11_eq, comparator_12_eq, comparator_13_eq, D_t, not_1_out, not_2_out, not_3_out, not_4_out,
       not_5_out, not_6_out, not_7_out, not_9_out, not_10_out, not_11_out, not_12_out, not_13_out,
       not_14_out, not_15_out, not_16_out, not_17_out, not_18_out, not_19_out, not_20_out, not_21_out,
       not_22_out, not_23_out, not_24_out, not_25_out, not_27_out, not_29_out, not_30_out, not_31_out,
       not_32_out, not_33_out, not_34_out, not_36_out, not_37_out, not_38_out, not_40_out, not_42_out,
       not_46_out, not_47_out, not_48_out, not_49_out, not_50_out, not_51_out, not_52_out, not_53_out,
       not_54_out, not_56_out, not_58_out, not_59_out, not_60_out, not_61_out, not_62_out, not_63_out,
       not_64_out, not_65_out, not_68_out, not_69_out, not_71_out, not_72_out, not_73_out, not_74_out,
       or_2_out, or_3_out, or_4_out, or_5_out, or_6_out, or_8_out, or_9_out, or_10_out, or_11_out, or_12_out,
       or_13_out, or_15_out, or_19_out, or_21_out, or_22_out, or_23_out, or_24_out, or_25_out, or_26_out,
       or_27_out, or_28_out, or_29_out, or_30_out, or_31_out, or_32_out, or_37_out, or_38_out, or_39_out,
       or_40_out;

  Clock #(.highDuration(1), .lowDuration(1)) clock_1 (.out(clock_1_out));
  Button button_1 (.out(button_1_out));
  Clock #(.highDuration(1), .lowDuration(1)) clock_2 (.out(clock_2_out));
  Button button_2 (.out(button_2_out));
  Clock #(.highDuration(1), .lowDuration(1)) clock_3 (.out(clock_3_out));
  Button button_3 (.out(button_3_out));
  Clock #(.highDuration(1), .lowDuration(1)) clock_4 (.out(clock_4_out));
  Button button_4 (.out(button_4_out));
  Clock #(.highDuration(1), .lowDuration(1)) clock_5 (.out(clock_5_out));
  Button button_5 (.out(button_5_out));
  Clock #(.highDuration(1), .lowDuration(1)) clock_6 (.out(clock_6_out));
  Button button_6 (.out(button_6_out));
  // Probe on A_t
  // Probe on A_t
  // Probe on A_t
  // Probe on D_t
  Counter #(.width(3), .max('h7), .ongoal("wrap"), .trigger("rising"), .behavior("new")) counter_1 (
    .Q({3{A_t}}), .clk(clock_1_out), .clr(button_1_out));  // open: load, D, count, carry, preset, down
  Counter #(.width(2), .max('h3), .ongoal("wrap"), .trigger("rising"), .behavior("new")) counter_2 (
    .Q({2{A_t}}), .clk(clock_2_out), .clr(button_2_out));  // open: load, D, count, carry, preset, down
  // Probe on A_t
  // Probe on A_t
  Counter #(.width(2), .max('h3), .ongoal("wrap"), .trigger("rising"), .behavior("new")) counter_3 (
    .Q({2{A_t}}), .clk(clock_3_out), .clr(button_3_out));  // open: load, D, count, carry, preset, down
  // Probe on A_t
  // Probe on A_t
  Counter #(.width(2), .max('h3), .ongoal("wrap"), .trigger("rising"), .behavior("new")) counter_4 (
    .Q({2{A_t}}), .clk(clock_4_out), .clr(button_4_out));  // open: load, D, count, carry, preset, down
  // Probe on A_t
  // Probe on A_t
  // Probe on A_t
  Counter #(.width(3), .max('h7), .ongoal("wrap"), .trigger("rising"), .behavior("new")) counter_5 (
    .Q({3{A_t}}), .clk(clock_5_out), .clr(button_5_out));  // open: load, D, count, carry, preset, down
  // Probe on A_t
  // Probe on A_t
  // Probe on A_t
  // Probe on D_t
  Counter #(.width(4), .max('hf), .ongoal("wrap"), .trigger("rising"), .behavior("new")) counter_6 (
    .Q({{3{A_t}}, D_t}), .clk(clock_6_out), .clr(button_6_out));  // open: load, D, count, carry, preset, down
  // Probe on A_t
  // Probe on A_t
  // Probe on A_t
  // Probe on A_t
  // Probe on A_t
  not not_1 (not_1_out, A_t);
  not not_2 (not_2_out, A_t);
  // Probe on X
  // Probe on Y
  // Probe on Z
  // Probe on A_t
  // Probe on A_t
  // Probe on A_t
  // Probe on A_t
  // Probe on A_t
  // Probe on A_t
  // Probe on D_t
  // Probe on A_t
  // Probe on A_t
  // Probe on A_t
  // Probe on A_t
  // Probe on A_t
  // Probe on A_t
  // Probe on A_t
  not not_3 (not_3_out, A_t);
  not not_4 (not_4_out, A_t);
  // Probe on A_t
  // Probe on A_t
  not not_5 (not_5_out, A_t);
  not not_6 (not_6_out, A_t);
  not not_7 (not_7_out, A_t);
  // NOT_Gate not_8 has open pins: in=A_t, out=open
  not not_9 (not_9_out, A_t);
  not not_10 (not_10_out, D_t);
  not not_11 (not_11_out, A_t);
  not not_12 (not_12_out, A_t);
  and and_1 (and_1_out, A_t, A_t);
  and and_2 (and_2_out, not_1_out, not_2_out);
  Comparator #(.width(1), .mode("twosComplement")) comparator_1 (.a(Y), .b(Z), .eq(comparator_1_eq));  // open: gt, lt
  not not_13 (not_13_out, A_t);
  not not_14 (not_14_out, A_t);
  not not_15 (not_15_out, A_t);
  not not_16 (not_16_out, A_t);
  not not_17 (not_17_out, A_t);
  not not_18 (not_18_out, A_t);
  not not_19 (not_19_out, A_t);
  not not_20 (not_20_out, A_t);
  not not_21 (not_21_out, A_t);
  and and_3 (and_3_out, A_t, A_t);
  not not_22 (not_22_out, and_3_out);
  and and_4 (and_4_out, not_3_out, not_4_out);
  not not_23 (not_23_out, and_4_out);
  not not_24 (not_24_out, A_t);
  not not_25 (not_25_out, A_t);
  // Buzzer #(.freq_measure("Hz"), .vol_width(7)) buzzer_1: pin names not known; wires that end beside it: buzzer_1_p1
  not not_26 (buzzer_1_p1, comparator_1_eq);
  LED #(.active("true")) led_1 (.in(comparator_1_eq));
  and and_5 (and_5_out, A_t, A_t);
  and and_6 (and_6_out, not_5_out, not_6_out, A_t);
  and and_7 (and_7_out, A_t, A_t);
  and and_8 (and_8_out, A_t, not_9_out, not_10_out);
  and and_9 (and_9_out, not_7_out, A_t);
  and and_10 (and_10_out, A_t, A_t, not_9_out, D_t);
  and and_11 (and_11_out, A_t, A_t);
  not not_27 (not_27_out, A_t);
  // NOT_Gate not_28 has open pins: in=A_t, out=open
  not not_29 (not_29_out, A_t);
  not not_30 (not_30_out, D_t);
  not not_31 (not_31_out, A_t);
  not not_32 (not_32_out, A_t);
  not not_33 (not_33_out, A_t);
  not not_34 (not_34_out, D_t);
  and and_12 (and_12_out, A_t, not_12_out);
  and and_13 (and_13_out, A_t, not_11_out);
  or or_1 (out_21, and_1_out, and_2_out);
  or or_2 (or_2_out, A_t, A_t);
  or or_3 (or_3_out, not_24_out, not_25_out);
  or or_4 (or_4_out, X, Y);
  or or_5 (or_5_out, X, Z);
  and and_14 (and_14_out, X, Y);
  and and_15 (and_15_out, X, Z);
  and and_16 (and_16_out, not_13_out, A_t);
  and and_17 (and_17_out, A_t, A_t);
  or or_6 (or_6_out, and_8_out, and_9_out);
  and and_18 (and_18_out, A_t, A_t);
  and and_19 (and_19_out, A_t, not_14_out);
  and and_20 (and_20_out, A_t, not_16_out);
  and and_21 (and_21_out, not_15_out, not_17_out);
  or or_7 (out_17, and_12_out, and_13_out);
  or or_8 (or_8_out, not_18_out, not_19_out);
  or or_9 (or_9_out, A_t, A_t);
  or or_10 (or_10_out, not_20_out, not_21_out);
  or or_11 (or_11_out, A_t, A_t);
  not not_35 (out_25, or_12_out);
  or or_12 (or_12_out, not_22_out, not_23_out);
  Comparator #(.width(1), .mode("twosComplement")) comparator_2 (
    .a(or_4_out), .b(or_5_out), .eq(out_27));  // open: gt, lt
  Comparator #(.width(1), .mode("twosComplement")) comparator_3 (
    .a(and_14_out), .b(and_15_out), .eq(out_28));  // open: gt, lt
  or or_13 (or_13_out, and_5_out, and_6_out);
  or or_14 (out_30, and_16_out, and_17_out);
  or or_15 (or_15_out, or_6_out, and_10_out);
  and and_22 (and_22_out, not_27_out, A_t, not_29_out, not_30_out);
  and and_23 (and_23_out, not_27_out, A_t, not_29_out, D_t);
  and and_24 (and_24_out, not_27_out, A_t, A_t, not_30_out);
  and and_25 (and_25_out, not_27_out, A_t, A_t, D_t);
  and and_26 (and_26_out, A_t, A_t, not_29_out, not_30_out);
  and and_27 (and_27_out, A_t, A_t, not_29_out, D_t);
  and and_28 (and_28_out, A_t, A_t, A_t, not_30_out);
  and and_29 (and_29_out, A_t, A_t, A_t, D_t);
  and and_30 (out_19, or_8_out, or_9_out);
  nand nand_1 (out_23, or_10_out, or_11_out);
  and and_31 (out_26, or_2_out, or_3_out);
  not not_36 (not_36_out, out_27);
  // Buzzer #(.freq_measure("Hz"), .vol_width(7)) buzzer_2: pin names not known; wires that end beside it: not_36_out
  LED #(.active("true")) led_2 (.in(out_27));
  not not_37 (not_37_out, out_28);
  // Buzzer #(.freq_measure("Hz"), .vol_width(7)) buzzer_3: pin names not known; wires that end beside it: not_37_out, out_28
  LED #(.active("true")) led_3 (.in(out_28));
  or or_16 (out_31, or_15_out, and_11_out);
  nor nor_1 (out_13, and_18_out, and_19_out);
  or or_17 (out_16, and_20_out, and_21_out);
  Comparator #(.width(1), .mode("twosComplement")) comparator_4 (
    .a(out_21), .b(out_23), .eq(comparator_4_eq));  // open: gt, lt
  Comparator #(.width(1), .mode("twosComplement")) comparator_5 (
    .a(out_25), .b(out_26), .eq(comparator_5_eq));  // open: gt, lt
  or or_18 (out_29, and_7_out, or_13_out);
  or or_19 (or_19_out, not_31_out, not_32_out, not_33_out, not_34_out);
  or or_20 (or_19_out, not_31_out, not_32_out, not_33_out, D_t);
  or or_21 (or_21_out, not_31_out, not_32_out, A_t, not_34_out);
  or or_22 (or_22_out, not_31_out, not_32_out, A_t, D_t);
  or or_23 (or_23_out, A_t, not_32_out, not_33_out, not_34_out);
  or or_24 (or_24_out, A_t, not_32_out, not_33_out, D_t);
  or or_25 (or_25_out, A_t, not_32_out, A_t, D_t);
  or or_26 (or_26_out, A_t, not_32_out, A_t, not_34_out);
  Comparator #(.width(1), .mode("twosComplement")) comparator_6 (
    .a(out_17), .b(out_19), .eq(comparator_6_eq));  // open: gt, lt
  not not_38 (not_38_out, comparator_4_eq);
  LED #(.active("true")) led_4 (.in(comparator_4_eq));
  or or_27 (or_27_out, and_22_out, and_23_out, and_24_out, and_25_out, and_26_out, and_27_out, and_28_out, and_29_out);
  Comparator #(.width(1), .mode("twosComplement")) comparator_7 (
    .a(out_13), .b(out_16), .eq(comparator_7_eq));  // open: gt, lt
  // Buzzer #(.freq_measure("Hz"), .vol_width(7)) buzzer_4: pin names not known; wires that end beside it: not_38_out
  // Buzzer #(.freq_measure("Hz"), .vol_width(7)) buzzer_5: pin names not known; wires that end beside it: buzzer_5_p1
  not not_39 (buzzer_5_p1, comparator_5_eq);
  LED #(.active("true")) led_5 (.in(comparator_5_eq));
  not not_40 (not_40_out, comparator_8_eq);
  Comparator #(.width(1), .mode("twosComplement")) comparator_8 (
    .a(out_29), .b(out_30), .eq(comparator_8_eq));  // open: gt, lt
  LED #(.active("true")) led_6 (.in(comparator_8_eq));
  Comparator #(.width(1), .mode("twosComplement")) comparator_9 (
    .a(out_31), .b(or_27_out), .eq(comparator_9_eq));  // open: gt, lt
  not not_41 (out_32, or_27_out);
  not not_42 (not_42_out, comparator_7_eq);
  // Buzzer #(.freq_measure("Hz"), .vol_width(7)) buzzer_6: pin names not known; wires that end beside it: not_42_out
  LED #(.active("true")) led_7 (.in(comparator_7_eq));
  // Buzzer #(.freq_measure("Hz"), .vol_width(7)) buzzer_7: pin names not known; wires that end beside it: buzzer_7_p1
  not not_43 (buzzer_7_p1, comparator_6_eq);
  LED #(.active("true")) led_8 (.in(comparator_6_eq));
  // Buzzer #(.freq_measure("Hz"), .vol_width(7)) buzzer_8: pin names not known; wires that end beside it: not_40_out
  // Buzzer #(.freq_measure("Hz"), .vol_width(7)) buzzer_9: pin names not known; wires that end beside it: buzzer_9_p1
  not not_44 (buzzer_9_p1, comparator_9_eq);
  LED #(.active("true")) led_9 (.in(comparator_9_eq));
  Comparator #(.width(1), .mode("twosComplement")) comparator_10 (
    .a(out_32), .b(and_32_out), .eq(comparator_10_eq));  // open: gt, lt
  and and_32 (and_32_out, or_19_out, or_19_out, or_21_out, or_22_out, or_23_out, or_24_out, or_25_out, or_26_out);
  // Buzzer #(.freq_measure("Hz"), .vol_width(7)) buzzer_10: pin names not known; wires that end beside it: buzzer_10_p1
  not not_45 (buzzer_10_p1, comparator_10_eq);
  LED #(.active("true")) led_10 (.in(comparator_10_eq));
  Clock #(.highDuration(1), .lowDuration(1)) clock_7 (.out(clock_7_out));
  Button button_7 (.out(button_7_out));
  Clock #(.highDuration(1), .lowDuration(1)) clock_8 (.out(clock_8_out));
  Button button_8 (.out(button_8_out));
  // Probe on A_t
  // Probe on A_t
  // Probe on A_t
  // Probe on D_t
  Counter #(.width(4), .max('hf), .ongoal("wrap"), .trigger("rising"), .behavior("new")) counter_7 (
    .Q({{3{A_t}}, D_t}), .clk(clock_7_out), .clr(button_7_out));  // open: load, D, count, carry, preset, down
  // Probe on A_t
  // Probe on A_t
  // Probe on A_t
  Counter #(.width(3), .max('h7), .ongoal("wrap"), .trigger("rising"), .behavior("new")) counter_8 (
    .Q({3{A_t}}), .clk(clock_8_out), .clr(button_8_out));  // open: load, D, count, carry, preset, down
  // Probe on A
  // Probe on A_t
  // Probe on A_t
  // Probe on A_t
  not not_46 (not_46_out, A_t);
  not not_47 (not_47_out, A_t);
  not not_48 (not_48_out, A_t);
  // Probe on A_t
  // Probe on A_t
  // Probe on A_t
  // Probe on D_t
  not not_49 (not_49_out, A_t);
  not not_50 (not_50_out, A_t);
  not not_51 (not_51_out, A_t);
  and and_33 (and_33_out, not_46_out, not_47_out);
  and and_34 (and_34_out, not_46_out, not_48_out, D_t);
  and and_35 (and_35_out, A_t, A_t);
  and and_36 (and_36_out, A_t, not_48_out);
  not not_52 (not_52_out, A_t);
  not not_53 (not_53_out, A_t);
  not not_54 (not_54_out, A_t);
  // NOT_Gate not_55 has open pins: in=D_t, out=open
  and and_37 (and_37_out, A_t, not_50_out);
  and and_38 (and_38_out, not_49_out, A_t);
  and and_39 (and_39_out, A_t, not_50_out);
  and and_40 (and_40_out, not_49_out, A_t);
  or or_28 (or_28_out, and_37_out, and_38_out);
  or or_29 (or_29_out, and_39_out, and_40_out);
  not not_56 (not_56_out, or_29_out);
  and and_41 (and_41_out, not_52_out, not_53_out);
  and and_42 (and_42_out, A_t, not_54_out);
  and and_43 (and_43_out, A_t, A_t);
  and and_44 (and_44_out, not_52_out, not_54_out, D_t);
  and and_45 (and_45_out, or_28_out, not_51_out);
  and and_46 (and_46_out, A_t, A_t);
  and and_47 (and_47_out, A_t, A_t);
  and and_48 (and_48_out, A_t, A_t);
  // NOT_Gate not_57 has open pins: in=A, out=open
  not not_58 (not_58_out, B);
  not not_59 (not_59_out, C);
  not not_60 (not_60_out, D);
  not not_61 (not_61_out, A_2);
  not not_62 (not_62_out, B_2);
  not not_63 (not_63_out, C_2);
  not not_64 (not_64_out, D_2);
  and and_49 (out_18, and_45_out, not_56_out);
  not not_65 (not_65_out, or_30_out);
  or or_30 (or_30_out, and_46_out, and_47_out, and_48_out);
  or or_31 (or_31_out, A_t, A_t, A_t);
  or or_32 (or_32_out, and_33_out, and_34_out, and_35_out, and_36_out);
  or or_33 (out_15, and_41_out, and_42_out, and_43_out, and_44_out);
  and and_50 (and_50_out, not_65_out, or_31_out);
  and and_51 (and_51_out, A_t, A_t, A_t);
  and and_52 (and_52_out, A_2, not_63_out);
  and and_53 (and_53_out, not_62_out, not_63_out);
  and and_54 (and_54_out, A_2, B_2, not_64_out);
  and and_55 (and_55_out, not_61_out, C_2, not_64_out);
  Comparator #(.width(1), .mode("twosComplement")) comparator_11 (
    .a(or_32_out), .b(out_15), .eq(comparator_11_eq));  // open: gt, lt
  and and_56 (and_56_out, not_58_out, not_59_out);
  and and_57 (and_57_out, A, not_59_out, D);
  and and_58 (and_58_out, C, not_60_out);
  not not_66 (out_12, or_32_out);
  // Buzzer #(.freq_measure("Hz"), .vol_width(7)) buzzer_11: pin names not known; wires that end beside it: buzzer_11_p1
  not not_67 (buzzer_11_p1, comparator_11_eq);
  LED #(.active("true")) led_11 (.in(comparator_11_eq));
  or or_34 (out_20, and_50_out, and_51_out);
  or or_35 (out_22, and_56_out, and_57_out, and_58_out);
  or or_36 (out_24, and_52_out, and_53_out, and_54_out, and_55_out);
  Comparator #(.width(1), .mode("twosComplement")) comparator_12 (
    .a(out_18), .b(out_20), .eq(comparator_12_eq));  // open: gt, lt
  not not_68 (not_68_out, comparator_12_eq);
  not not_69 (not_69_out, out_22);
  // Buzzer #(.freq_measure("Hz"), .vol_width(7)) buzzer_12: pin names not known; wires that end beside it: not_69_out
  LED #(.active("true")) led_12 (.in(out_22));
  // Buzzer #(.freq_measure("Hz"), .vol_width(7)) buzzer_13: pin names not known; wires that end beside it: buzzer_13_p1
  not not_70 (buzzer_13_p1, out_24);
  LED #(.active("true")) led_13 (.in(out_24));
  // Buzzer #(.freq_measure("Hz"), .vol_width(7)) buzzer_14: pin names not known; wires that end beside it: not_68_out
  LED #(.active("true")) led_14 (.in(comparator_12_eq));
  Clock #(.highDuration(1), .lowDuration(1)) clock_9 (.out(clock_9_out));
  Button button_9 (.out(button_9_out));
  Counter #(.width(4), .max('hf), .ongoal("wrap"), .trigger("rising"), .behavior("new")) counter_9 (
    .Q({{3{A_t}}, D_t}), .clk(clock_9_out), .clr(button_9_out));  // open: load, D, count, carry, preset, down
  // Probe on A_t
  // Probe on A_t
  // Probe on A_t
  // Probe on D_t
  not not_71 (not_71_out, A_t);
  not not_72 (not_72_out, A_t);
  not not_73 (not_73_out, A_t);
  not not_74 (not_74_out, D_t);
  or or_37 (or_37_out, A_t, A_t);
  or or_38 (or_38_out, not_72_out, A_t);
  or or_39 (or_39_out, not_71_out, not_73_out);
  or or_40 (or_40_out, A_t, A_t, not_74_out);
  and and_59 (out_14, or_37_out, or_38_out, or_39_out, or_40_out);
  Comparator #(.width(1), .mode("twosComplement")) comparator_13 (
    .a(out_12), .b(out_14), .eq(comparator_13_eq));  // open: gt, lt
  // Buzzer #(.freq_measure("Hz"), .vol_width(7)) buzzer_15: pin names not known; wires that end beside it: buzzer_15_p1
  not not_75 (buzzer_15_p1, comparator_13_eq);
  LED #(.active("true")) led_15 (.in(comparator_13_eq));

  // Other names for the same wires on the sheet: B_t = A_t; C_t = A_t

  // Notes on the sheet:
  //   2.4 (1)
  //   2.6
  //   2.7 (1)
  //   2.2 (1)
  //   2.3 (1)
  //   2.5
  //   不用做
  //   2.10 (1)
  //   2.8 (1)
  //   2.9 (1)
  //   不用做
endmodule
